# Fritzing sketch Łazienka Rymanowska (saved by Fritzing 0.9.3b)

parts:
  F2 = Fan - Ventilador [package=THT]
  WeMos_D1_Mini4 = WeMos D1 Mini
  M3 = BME280
  2_Channel_Relay2 = 2 Channel Power Relay
  PIR2 = PIR sensor
  R3 = Photocell (LDR) [package=THT]
  R4 = Resistor [tolerance=±5% resistance=220 package="0805 [SMD]"]
  Q2 = Basic FET N-Channel [package="TO220 [THT]"]
  LED2 = LEDs [package=led10mm]

nets:
  N1: F2.GND, 2_Channel_Relay2.K1-NO
  3V3: WeMos_D1_Mini4.3V3, M3.VIN, 2_Channel_Relay2.VCC, PIR2.VDD, R3.pin_1
  N2: WeMos_D1_Mini4.5V, LED2.A
  N3: WeMos_D1_Mini4.A0, R3.pin_0, R4.Pin_1
  N4: WeMos_D1_Mini4.D1, M3.SCL
  N5: WeMos_D1_Mini4.D2, M3.SDA
  N6: WeMos_D1_Mini4.D5, 2_Channel_Relay2.IN1
  N7: WeMos_D1_Mini4.D6, 2_Channel_Relay2.IN2
  N8: WeMos_D1_Mini4.D7, PIR2.SIG
  N9: WeMos_D1_Mini4.D8, Q2.gate
  GND: WeMos_D1_Mini4.G, M3.GND, 2_Channel_Relay2.GND, PIR2.GND, R4.Pin_0, Q2.source
  N10: Q2.drain, LED2.C

notes:
  Łazienka Rymanowska
  N
  L
  BME280
  Kocioł CO
  Wentylator
  Przekaźniki
  PIR Sensor
  AM312
  Wemos D1
  Photoresistor
  MOSFET
  BathFan = D5; //Deklaracja pinu na który zostanie wysłany sygnał załączenia wentylatora
  Piec_CO = D6; //Deklaracja pinu na którym będzie włączany piec CO
  PIR_Sensor = D7; //Deklaracja pinu z sensorem ruchu AM312
  LED_Light = D8; //Deklaracja pinu z MOSFETem do illuminacji sedesu

custom parts:
  Fan - Ventilador: Ventilador de 2 pines, se encuentra comunmente en computadoras de escritorio
  BME280: Temperature Humidity Barometric presure Sensor
  2 Channel Power Relay: A 2 channel power relay. The module operates at 5V.
