# Fritzing sketch Pokój Rymanowska (saved by Fritzing 0.9.3b)

parts:
  WeMos_D1_Mini3 = WeMos D1 Mini
  OLED_I2C2 = OLED 128x64 I2C Monochrome Display
  Capacitive_Sol_Moisture_Sensor_V1_2 = Capacitive Sol Moisture Sensor V1.0
  M2 = BME280

nets:
  3V3: WeMos_D1_Mini3.3V3, OLED_I2C2.VDD, Capacitive_Sol_Moisture_Sensor_V1_2.VCC, M2.VIN
  N1: WeMos_D1_Mini3.A0, Capacitive_Sol_Moisture_Sensor_V1_2.A
  N2: WeMos_D1_Mini3.D1, OLED_I2C2.SCK, M2.SCL
  N3: WeMos_D1_Mini3.D2, OLED_I2C2.SDA, M2.SDA
  GND: WeMos_D1_Mini3.G, OLED_I2C2.GND, Capacitive_Sol_Moisture_Sensor_V1_2.GND, M2.GND

notes:
  Pokój Rymanowska
  Wemos D1
  BME280
  OLED 0,96"
  128x64
  Czujnik wilgotności gleby

custom parts:
  Capacitive Sol Moisture Sensor V1.0: Soild moisture sensor developed by DFROBOT. It is resistant to corrosion.
  BME280: Temperature Humidity Barometric presure Sensor
